# Fritzing sketch p3_bottone (saved by Fritzing 0.9.3b)
breadboards: 1

parts:
  Componente1 = Arduino Uno (Rev3)
  S1 = Pushbutton [package="[THT]"]
  R1 = Resistor [tolerance=±5% resistance=220 package=THT]
  LED1 = LED - 5mm [color="Red (633nm)" package="5 mm [THT]"]
  R2 = Resistor [tolerance=±5% resistance=220 package=THT]

nets:
  N1: Componente1.D13/SCK, R2.Pin_1
  N2: Componente1.GND, R1.Pin_0, LED1.cathode
  N3: Componente1.D2, Componente1.5V, S1.Pin_1, S1.Pin_2
  N4: S1.Pin_3, S1.Pin_4, R1.Pin_1
  N5: LED1.anode, R2.Pin_0
